// Logisim project pchecker.circ as structural Verilog: 1 circuit, main circuit main
module main (
  input  in_1,
  output out_2
);

  wire clock_1_out, main_1_q0, main_1_q1, main_1_q2, main_1_q3;

  Clock clock_1 (.out(clock_1_out));
  contadorcresc_main main_1 (
    .CLK(clock_1_out), .RST(in_1), .Q0(main_1_q0), .Q1(main_1_q1), .Q2(main_1_q2), .Q3(main_1_q3));
  parity_main main_2 (.B0(main_1_q0), .B1(main_1_q1), .B2(main_1_q2), .B3(main_1_q3), .P(out_2));

  // Notes on the sheet:
  //   código realizado por João Paulo Ferrari Sant'Ana dia 11/11/24 as 22:17
  //   arquivo "parity" realizado pelo professor CESAR GIACOMINI PENTEADO
endmodule
