// Logisim project regress.circ as structural Verilog: 1 circuit, main circuit main
module main (
  input  gambiarra,
  input  RST,
  input  PST
);

  wire CLK_out, decodiicador7seg_1_a_2, decodiicador7seg_1_b_2, decodiicador7seg_1_c_2,
       decodiicador7seg_1_d_2, decodiicador7seg_1_e, decodiicador7seg_1_f, decodiicador7seg_1_g, main_1_q0,
       main_1_q1, main_1_q2, \se_não_houver_mais_energia_acenda_a_lampâda_out ;

  Clock CLK (.out(CLK_out));
  contagemregress_main main_1 (.CLK(CLK_out), .RST(RST), .PST(PST), .Q0(main_1_q0), .Q1(main_1_q1), .Q2(main_1_q2));
  nor \se_não_houver_mais_energia_acenda_a_lampâda  (\se_não_houver_mais_energia_acenda_a_lampâda_out , main_1_q1, main_1_q0, main_1_q2);
  LED led_1 (.in(\se_não_houver_mais_energia_acenda_a_lampâda_out ));
  DECODIICADOR7SEG decodiicador7seg_1 (
    .A(gambiarra), .B(main_1_q2), .C(main_1_q1), .D(main_1_q0), .a_2(decodiicador7seg_1_a_2),
    .b_2(decodiicador7seg_1_b_2), .c_2(decodiicador7seg_1_c_2), .d_2(decodiicador7seg_1_d_2),
    .e(decodiicador7seg_1_e), .f(decodiicador7seg_1_f), .g(decodiicador7seg_1_g));
  _7_Segment_Display u_7_segment_display_1 (
    .g(decodiicador7seg_1_g), .f(decodiicador7seg_1_f), .a(decodiicador7seg_1_a_2),
    .b(decodiicador7seg_1_b_2), .e(decodiicador7seg_1_e), .d(decodiicador7seg_1_d_2),
    .c(decodiicador7seg_1_c_2));  // open: dp

  // Notes on the sheet:
  //   tá dando problema porque eu fiz 4 bit, ou seja, temos 15 números, sendo que esse relogio suporta só 9
endmodule
